# Fritzing sketch giga (saved by Fritzing 0.9.9b)
breadboards: 1

parts:
  J9 = Basic Servo
  J10 = Basic Servo
  J11 = Basic Servo
  Part13 = MD10C R2
  Part14 = MD10C R2
  Part15 = MD10C R2
  Part16 = MD10C R2
  Part17 = MD10C R2
  Part18 = MD10C R2
  A3 = Arduino GIGA R1 WiFi
  J12 = Basic Servo
  Power_plug3 = Power plug
  R5 = Resistor [tolerance=±5% resistance=220 package="0603 [SMD]"]
  R6 = Resistor [tolerance=±5% resistance=220 package="0603 [SMD]"]
  U4 = Voltage Regulator - Variable [package="TO220 [THT]"]
  C5 = Tantalum Capacitor [capacitance=1μF voltage=35V package="100 mil [THT, tantalum]"]
  C6 = Tantalum Capacitor [capacitance=1μF voltage=35V package="100 mil [THT, tantalum]"]
  D7 = Rectifier Diode [part_number=1N4001 package="300 mil [THT]"]
  D8 = Rectifier Diode [part_number=1N4001 package="300 mil [THT]"]
  Mod7 = TMC2209 [package=THT]
  Mod8 = TMC2209 [package=THT]
  Mod9 = TMC2209 [package=THT]
  Mod10 = TMC2209 [package=THT]
  Mod11 = TMC2209 [package=THT]
  A4 = Seeed wio-e5
  A5 = Raspberry Pi 5  # not connected
  A6 = AS5600 module
  A7 = AS5600 module
  A8 = AS5600 module
  A9 = AS5600 module
  A10 = AS5600 module
  Part19 = Adafruit AHT20 Temperature and Humidity Sensor [part_number="Adafruit #4566"]
  A11 = BMI160 breakout

nets:
  GND: J9.gnd, J10.gnd, J11.gnd, J12.gnd, Power_plug3.GND, R6.Pin_1, C5.-, C6.-
  VCC: J9.vcc, J10.vcc, J11.vcc, J12.vcc, R5.Pin_0, U4.OUT, C6.+, D7.anode, D8.cathode
  N1: J9.pulse, A3.Pin_101, A3.Pin_119
  N2: J10.pulse, A3.Pin_102, A3.Pin_120
  N3: J11.pulse, A3.Pin_103, A3.Pin_121
  N4: Part13.no_name_yet#connector_1, A3.Pin_113
  N5: Part13.no_name_yet#connector_2, A3.Pin_134
  N6: Part14.no_name_yet#connector_1, A3.Pin_96, A3.Pin_114
  N7: Part14.no_name_yet#connector_2, A3.Pin_135
  N8: Part15.no_name_yet#connector_1, A3.Pin_97, A3.Pin_115
  N9: Part15.no_name_yet#connector_2, A3.Pin_136
  N10: Part16.no_name_yet#connector_1, A3.Pin_98, A3.Pin_116
  N11: Part16.no_name_yet#connector_2, A3.Pin_137
  N12: Part17.no_name_yet#connector_1, A3.Pin_99, A3.Pin_117
  N13: Part17.no_name_yet#connector_2, A3.Pin_138
  N14: Part18.no_name_yet#connector_1, A3.Pin_100, A3.Pin_118
  N15: Part18.no_name_yet#connector_2, A3.Pin_139
  N16: A3.Pin_3, Mod8.Dir
  N17: A3.Pin_4, Mod8.Step
  N18: A3.Pin_5, Mod11.Dir
  N19: A3.Pin_6, Mod11.Step
  N20: A3.Pin_7, Mod11.EN
  N21: A3.Pin_8, Mod7.Dir
  N22: A3.Pin_9, A3.Pin_10, Mod7.Step
  N23: A3.Pin_13, Mod9.EN
  N24: A3.Pin_14, Mod9.Step
  N25: A3.Pin_15, Mod9.Dir
  N26: A3.Pin_16, Mod10.EN
  N27: A3.Pin_17, Mod10.Step
  N28: A3.Pin_18, Mod10.Dir
  N29: A3.Pin_19, Mod7.EN
  N30: A3.Pin_104, A3.Pin_122, J12.pulse
  N31: A3.Pin_124, A6.Pin_6, A7.Pin_6, A8.Pin_6, A9.Pin_6, A10.Pin_6
  N32: A3.Pin_125, A6.Pin_5, A7.Pin_5, A8.Pin_5, A9.Pin_5, A10.Pin_5
  N33: A3.Pin_132, A4.Pin_4
  N34: A3.Pin_133, A4.Pin_3
  N35: A3.Pin_148, Part19.SDA, A11.Pin_10
  N36: A3.Pin_149, Part19.SCL, A11.Pin_9
  N37: Power_plug3.VCC, U4.IN, D7.cathode
  N38: R5.Pin_1, R6.Pin_0, U4.ADJ, C5.+, D8.anode

custom parts:
  Arduino GIGA R1 WiFi: The Arduino GIGA R1 WiFi is designed for ambitious makers who want to step up their game.
  TMC2209: TMC2209-LA stepper motor controller and driver. Supply voltage 4.75-28V Iphase up to 1.77A rms (2.5A peak)
  Seeed wio-e5: text
  Raspberry Pi 5: The RPi5, a faster version of the awesome Raspberry Pi4B ARM Board with 40 pin gpio.
  AS5600 module: .This module is mainly placed behind the stepper motor to obtain the rotation angle of the stepper motor.
  Adafruit AHT20 Temperature and Humidity Sensor: The AHT20 is a nice but inexpensive temperature and humidity sensor from the same folks that brought us the DHT22. You can take sensor readings as often as you like, and it uses standard I2C so its super easy to use with any Arduino or Linux/Raspberry Pi board. This sensor has a typical accuracy of +- 2% relative humidity, and +-0.3 °C. There is only one I2C address so its not a good option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
  BMI160 breakout: BMI160 Latest Stance Accelerometer Gyroscope module 6 Dof inertial Measurement Sensors.
